# Fritzing sketch menoraboard (saved by Fritzing 1.0.4)
stripboards: 1

parts:
  R1 = Resistor [tolerance=±5% power=0.25 resistance=220 package=THT]
  R2 = Resistor [tolerance=±5% power=0.25 resistance=220 package=THT]
  R3 = Resistor [tolerance=±5% power=0.25 resistance=220 package=THT]
  R4 = Resistor [tolerance=±5% power=0.25 resistance=220 package=THT]
  R5 = Resistor [tolerance=±5% power=0.25 resistance=220 package=THT]
  R6 = Resistor [tolerance=±5% power=0.25 resistance=220 package=THT]
  R7 = Resistor [tolerance=±5% power=0.25 resistance=220 package=THT]
  R8 = Resistor [tolerance=±5% power=0.25 resistance=220 package=THT]
  R9 = Resistor [tolerance=±5% power=0.25 resistance=220 package=THT]
  R10 = Resistor [tolerance=±5% power=0.25 resistance=220 package=THT]
  R11 = Resistor [tolerance=±5% power=0.25 resistance=220 package=THT]
  R12 = Resistor [tolerance=±5% power=0.25 resistance=220 package=THT]
  R13 = Resistor [tolerance=±5% power=0.25 resistance=220 package=THT]
  R14 = Resistor [tolerance=±5% power=0.25 resistance=220 package=THT]
  R15 = Resistor [tolerance=±5% power=0.25 resistance=220 package=THT]
  R16 = Resistor [tolerance=±5% power=0.25 resistance=220 package=THT]
  R17 = Resistor [tolerance=±5% power=0.25 resistance=220 package=THT]
  R18 = Resistor [tolerance=±5% power=0.25 resistance=220 package=THT]
  R19 = Resistor [tolerance=±5% power=0.25 resistance=220 package=THT]
  R20 = Resistor [tolerance=±5% power=0.25 resistance=220 package=THT]
  R21 = Resistor [tolerance=±5% power=0.25 resistance=220 package=THT]
  R22 = Resistor [tolerance=±5% power=0.25 resistance=220 package=THT]
  R23 = Resistor [tolerance=±5% power=0.25 resistance=220 package=THT]
  R24 = Resistor [tolerance=±5% power=0.25 resistance=220 package=THT]
  R25 = Resistor [tolerance=±5% power=0.25 resistance=220 package=THT]
  R26 = Resistor [tolerance=±5% power=0.25 resistance=220 package=THT]
  R27 = Resistor [tolerance=±5% power=0.25 resistance=220 package=THT]
  U1 = 74HC595 [package="DIP16 [THT]"]
  U2 = 74HC595 [package="DIP16 [THT]"]
  U3 = 74HC595 [package="DIP16 [THT]"]
  U4 = 74HC595 [package="DIP16 [THT]"]
  A1 = Raspberry Pi Pico W
  Q2 = NPN-Transistor [package="TO92 [THT]"]
  Q3 = NPN-Transistor [package="TO92 [THT]"]
  Q4 = NPN-Transistor [package="TO92 [THT]"]
  Q5 = NPN-Transistor [package="TO92 [THT]"]
  Q6 = NPN-Transistor [package="TO92 [THT]"]
  Q7 = NPN-Transistor [package="TO92 [THT]"]
  Q8 = NPN-Transistor [package="TO92 [THT]"]
  Q9 = NPN-Transistor [package="TO92 [THT]"]
  Q10 = NPN-Transistor [package="TO92 [THT]"]
  LED6 = RGB LED (com. cathode, rgb) [color="Red (633nm)" current=0.030A package="5 mm [THT]"]
  LED7 = RGB LED (com. cathode, rgb) [color="Red (633nm)" current=0.030A package="5 mm [THT]"]
  LED2 = RGB LED (com. cathode, rgb) [color="Red (633nm)" current=0.030A package="5 mm [THT]"]
  LED4 = RGB LED (com. cathode, rgb) [color="Red (633nm)" current=0.030A package="5 mm [THT]"]
  LED9 = RGB LED (com. cathode, rgb) [color="Red (633nm)" current=0.030A package="5 mm [THT]"]
  LED5 = RGB LED (com. cathode, rgb) [color="Red (633nm)" current=0.030A package="5 mm [THT]"]
  LED8 = RGB LED (com. cathode, rgb) [color="Red (633nm)" current=0.030A package="5 mm [THT]"]
  LED3 = RGB LED (com. cathode, rgb) [color="Red (633nm)" current=0.030A package="5 mm [THT]"]
  LED1 = RGB LED (com. cathode, rgb) [color="Red (633nm)" current=0.030A package="5 mm [THT]"]

nets:
  N1: R1.Pin_0, LED1.green_anode
  N2: R1.Pin_1, U2.Q7'
  N3: R2.Pin_0, LED1.red_anode
  N4: R2.Pin_1, U2.MR
  N5: R3.Pin_0, LED1.blue_anode
  N6: R3.Pin_1, U2.Q7
  N7: R4.Pin_0, LED2.green_anode
  N8: R4.Pin_1, U4.DS
  N9: R5.Pin_0, LED2.blue_anode
  N10: R5.Pin_1, U4.OE
  N11: R6.Pin_0, LED2.red_anode
  N12: R6.Pin_1, U4.Q0
  N13: R7.Pin_0, LED3.green_anode
  N14: R7.Pin_1, U4.SH_CP
  N15: R8.Pin_0, LED3.blue_anode
  N16: R8.Pin_1, U4.MR
  N17: R9.Pin_0, LED3.red_anode
  N18: R9.Pin_1, U4.ST_CP
  N19: R10.Pin_0, LED4.green_anode
  N20: R10.Pin_1, U1.MR
  N21: R11.Pin_0, LED6.blue_anode
  N22: R11.Pin_1, U1.ST_CP
  N23: R12.Pin_0, LED5.red_anode
  N24: R12.Pin_1, U4.Q7'
  N25: R13.Pin_0, LED6.red_anode
  N26: R13.Pin_1, U1.DS
  N27: R14.Pin_0, LED4.blue_anode
  N28: R14.Pin_1, U1.Q7'
  N29: R15.Pin_0, LED6.green_anode
  N30: R15.Pin_1, U1.OE
  N31: R16.Pin_0, LED4.red_anode
  N32: R16.Pin_1, U1.SH_CP
  N33: R17.Pin_0, LED5.blue_anode
  N34: R17.Pin_1, U1.Q0
  N35: R18.Pin_0, LED5.green_anode
  N36: R18.Pin_1, U4.Q7
  N37: R19.Pin_0, LED7.green_anode
  N38: R19.Pin_1, U3.Q7'
  N39: R20.Pin_0, LED9.blue_anode
  N40: R20.Pin_1, U3.SH_CP
  N41: R21.Pin_0, LED8.red_anode
  N42: R21.Pin_1, U1.Q7
  N43: R22.Pin_0, LED9.red_anode
  N44: R22.Pin_1, U3.OE
  N45: R23.Pin_0, LED7.blue_anode
  N46: R23.Pin_1, U3.Q7
  N47: R24.Pin_0, LED9.green_anode
  N48: R24.Pin_1, U3.ST_CP
  N49: R25.Pin_0, LED7.red_anode
  N50: R25.Pin_1, U3.MR
  N51: R26.Pin_0, LED8.blue_anode
  N52: R26.Pin_1, U3.DS
  N53: R27.Pin_0, LED8.green_anode
  N54: R27.Pin_1, U3.Q0
  N55: U1.Q1, U4.Q6
  GND: U1.Q2, U1.GND, U2.Q2, U2.GND, U3.Q2, U3.GND, U4.Q2, U4.GND, A1.pin_39
  N56: U1.Q3, U2.Q3, U3.Q3, U4.Q3, A1.pin_7
  N57: U1.Q4, U2.Q4, U3.Q4, U4.Q4, A1.pin_6
  VCC: U1.Q5, U1.VCC, U2.Q5, U2.VCC, U3.Q5, U3.VCC, U4.Q5, U4.VCC, A1.pin_3, A1.pin_8, A1.pin_13, A1.pin_18, A1.pin_23, A1.pin_28, A1.pin_33, A1.pin_38, Q2.E, Q3.E, Q4.E, Q5.E, Q6.E, Q7.E, Q8.E, Q9.E, Q10.E
  N58: U1.Q6, U3.Q1
  N59: U2.Q6, U4.Q1
  N60: U3.Q6, A1.pin_4
  N61: A1.pin_10, Q10.C
  N62: A1.pin_11, Q9.C
  N63: A1.pin_12, Q8.C
  N64: A1.pin_14, Q7.C
  N65: A1.pin_15, Q6.C
  N66: A1.pin_16, Q5.C
  N67: A1.pin_17, Q4.C
  N68: A1.pin_19, Q3.C
  N69: A1.pin_20, Q2.C
  N70: Q2.B, LED1.common_cathode
  N71: Q3.B, LED2.common_cathode
  N72: Q4.B, LED3.common_cathode
  N73: Q5.B, LED5.common_cathode
  N74: Q6.B, LED6.common_cathode
  N75: Q7.B, LED4.common_cathode
  N76: Q8.B, LED8.common_cathode
  N77: Q9.B, LED9.common_cathode
  N78: Q10.B, LED7.common_cathode

custom parts:
  Raspberry Pi Pico W: Raspberry Pi Pico W. Based around the RP2040 microcontroller the Pico W is a low cost microcontroller device bringing Raspberry Pi quality, cost, and easy of use to the microcontroller space. The areas marked KEEPOUT in pcb silkscreen should not have traces running through them to avoid shorts on a soldered in module!
